# Fritzing sketch basil (saved by Fritzing 0.9.0b)
breadboards: 1

parts:
  Part1 = Photon
  T1 = LM35 Temperature Sensor [package="TO92 [THT]"]
  SW1 = DIP Switch 8 Position [package=dipswitch-08]

nets:
  N1: Part1.A0, T1.Vout
  N2: Part1.WKP, SW1.1
  GND: Part1.GND, T1.GND
  N3: Part1.VIN, T1.+Vs
  N4: Part1.D2, SW1.2
  N5: Part1.3V3, SW1.15, SW1.16
